# Fritzing sketch tetris_wiring (saved by Fritzing 0.9.3b)
breadboards: 1

parts:
  Mod1 = Raspberry Pi Pico
  Part1 = OLED Monochrome 128x64 0.96 inch [part_number=326]
  S1 = Momentary Switch [package=ksa_sealed_tac_switch]
  S2 = Momentary Switch [package=ksa_sealed_tac_switch]
  S3 = Momentary Switch [package=ksa_sealed_tac_switch]
  S4 = Momentary Switch [package=ksa_sealed_tac_switch]

nets:
  N1: Mod1.pin_3, Mod1.pin_8, Mod1.pin_13, Mod1.pin_18, Mod1.pin_23, Mod1.pin_28, Mod1.pin_33, Mod1.pin_38, Part1.CS, Part1.GND
  N2: Mod1.pin_4, Part1.SCLK_SCK
  N3: Mod1.pin_5, Part1.MOSI_SDA
  N4: Mod1.pin_6, Part1.DC_SA0
  N5: Mod1.pin_7, Part1.RESET
  N6: Mod1.pin_24, S1.2
  N7: Mod1.pin_25, S2.2
  N8: Mod1.pin_26, S3.2
  N9: Mod1.pin_27, S4.2
  N10: Mod1.pin_36, Part1.3.3V, S1.3, S2.3, S3.3, S4.3

custom parts:
  Raspberry Pi Pico: Raspberry Pi Pico. Based around the RP2040 microcontroller the Pico is a low cost microcontroller device bringing Raspberry Pi quality, cost, and easy of use to the microcontroller space. Jan 2021, Split part in to two versions: tht (this one) and SMD. This one will drill holes for a .1 in header in pcb to allow plugging in the module as well as providing pads to solder the module to the top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
  OLED Monochrome 128x64 0.96 inch: These displays are small, only about 1" diameter, but very readable due to the high contrast of an OLED display. This display is made of 128x64 individual white OLED pixels, each one is turned on or off by the controller chip. Because the display makes its own light, no backlight is required. This reduces the power required to run the OLED and is why the display has such high contrast; we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
